// Logisim project ex4.circ as structural Verilog: 1 circuit, main circuit Split
module Split (
  input  [7:0] In1,
  output Out1,
  output [7:0] Out2
);

  wire not_2_out;
  wire [7:0] Neg2, not_1_out;
  wire [7:7] Neg;

  assign not_1_out = ~{Neg[7], In1[6:0]};  // NOT_Gate not_1, 8 bits wide
  Adder adder_1 (.a(not_1_out), .b(8'h1), .out(Neg2));  // open: cin, cout
  not not_2 (not_2_out, In1[7]);
  Multiplexer #(.enable("false")) multiplexer_1 (.in0(In1[7]), .in1(not_2_out), .out(Neg[7]), .sel(In1[7]));
  and and_1 (Out1, In1[0], In1[7]);
  Multiplexer #(.width(8), .enable("false")) multiplexer_2 (
    .in0({Neg[7], In1[6:0]}), .in1(Neg2), .out(Out2), .sel(In1[7]));

  // Other names for the same wires on the sheet: Last = In1[7]; Neg[6:0] = In1[6:0]; Zero = In1[0];
  //   Mid[5:0] = In1[6:1]; Result[7:0] = Out2

  // Notes on the sheet:
  //   PUT CIRCUITRY HERE
endmodule
